# Fritzing sketch assignment2 (saved by Fritzing 0.7.10b)
breadboards: 1

parts:
  Arduino1 = Arduino
  S1 = Pushbutton [package="[THT]"]
  S2 = Pushbutton [package="[THT]"]
  S3 = Pushbutton [package="[THT]"]
  S4 = Pushbutton [package="[THT]"]
  S5 = Pushbutton [package="[THT]"]
  LED1 = RGB LED - (4 legs) [package="5 mm [THT]"]
  LED2 = red smd LED [package="0603 [SMD]"]
  R1 = Resistor [tolerance=±5% resistance=220 package=THT]
  R2 = Resistor [tolerance=±5% resistance=220 package=THT]

nets:
  N1: Arduino1.D13, LED2.anode
  N2: Arduino1.D10, LED1.red_cathode
  N3: Arduino1.D9, LED1.common_anode
  N4: Arduino1.D8, LED1.green_cathode
  N5: Arduino1.D7, S1.Pin_1, S1.Pin_2
  N6: Arduino1.D6, S2.Pin_1, S2.Pin_2
  N7: Arduino1.D5, S3.Pin_1, S3.Pin_2
  N8: Arduino1.D4, S4.Pin_1, S4.Pin_2
  N9: Arduino1.D3, S5.Pin_1, S5.Pin_2
  N10: Arduino1.+5V, R1.Pin_1, R2.Pin_1
  N11: Arduino1.GND, S1.Pin_3, S1.Pin_4, S2.Pin_3, S2.Pin_4, S3.Pin_3, S3.Pin_4, S4.Pin_3, S4.Pin_4, S5.Pin_3, S5.Pin_4
  N12: LED1.blue_cathode, R1.Pin_0
  N13: LED2.cathode, R2.Pin_0
